# Fritzing sketch esquema_hardware_solo_directo_protoboard (saved by Fritzing 0.9.10b)
breadboards: 1

parts:
  Componente2 = Arduino Nano (Rev3.0) (ICSP)
  M1 = DC Motor [voltage_(max)=6V voltage_(min)=3V]  # not connected
  M2 = DC Motor [voltage_(max)=6V voltage_(min)=3V]  # not connected
  Componente5 = Motor Driver 1A Dual TB6612FNG  # not connected
  VCC1 = Battery block 9V
  HC-SR04_Sensor_1 = HC-SR04 Ultrasonic Distance Sensor
  HC-SR04_Sensor_2 = HC-SR04 Ultrasonic Distance Sensor
  Mod1 = Raspberry Pi 4B  # not connected

nets:
  N1: Componente2.D2, HC-SR04_Sensor_1.ECHO
  N2: Componente2.D3, HC-SR04_Sensor_1.TRIG
  N3: Componente2.D4, HC-SR04_Sensor_2.ECHO
  N4: Componente2.D5, HC-SR04_Sensor_2.TRIG
  VCC: Componente2.5V, HC-SR04_Sensor_1.VCC, HC-SR04_Sensor_2.VCC
  GND: VCC1.-, HC-SR04_Sensor_1.GND, HC-SR04_Sensor_2.GND
